// Logisim project project(332)23bit.circ as structural Verilog
module register_file_23 (
  input  [22:0] Write_data,
  input  Write_enabler,
  input  [4:0] RS,
  input  [4:0] RD,
  input  [4:0] RT,
  input  Clock,
  input  Clear,
  output [22:0] Data_1,
  output [22:0] Data_2
);

  wire and_1_out, and_2_out, and_3_out, and_4_out, and_5_out, and_6_out, and_7_out, and_8_out, and_9_out,
       and_10_out, and_11_out, and_12_out, and_13_out, and_14_out, and_15_out, and_16_out, and_17_out,
       and_18_out, and_19_out, and_20_out, and_21_out, and_22_out, and_23_out, decoder_1_out0,
       decoder_1_out1, decoder_1_out2, decoder_1_out3, decoder_1_out4, decoder_1_out5, decoder_1_out6,
       decoder_1_out7, decoder_1_out8, decoder_1_out9, decoder_1_out10, decoder_1_out11, decoder_1_out12,
       decoder_1_out13, decoder_1_out14, decoder_1_out15, decoder_1_out16, decoder_1_out17, decoder_1_out18,
       decoder_1_out19, decoder_1_out20, decoder_1_out21, decoder_1_out22;
  wire [22:0] _0_q, _1_q, _2_q, _3_q, _4_q, _5_q, _6_q, _7_q, _8_q, _9_q, _10_q, _11_q, _12_q, _13_q, _14_q,
       _15_q, _16_q, _17_q, _18_q, _19_q, _20_q, _21_q, _22_q;

  Decoder #(.select(5), .enable("false")) decoder_1 (
    .out0(decoder_1_out0), .out1(decoder_1_out1), .out2(decoder_1_out2), .out3(decoder_1_out3),
    .out4(decoder_1_out4), .out5(decoder_1_out5), .out6(decoder_1_out6), .out7(decoder_1_out7),
    .out8(decoder_1_out8), .out9(decoder_1_out9), .out10(decoder_1_out10), .out11(decoder_1_out11),
    .out12(decoder_1_out12), .out13(decoder_1_out13), .out14(decoder_1_out14), .out15(decoder_1_out15),
    .out16(decoder_1_out16), .out17(decoder_1_out17), .out18(decoder_1_out18), .out19(decoder_1_out19),
    .out20(decoder_1_out20), .out21(decoder_1_out21), .out22(decoder_1_out22), .sel(RD));  // open: out23, out24, out25, out26, out27, out28, out29, out30, out31
  and and_1 (and_1_out, Write_enabler, decoder_1_out0);
  and and_2 (and_2_out, Write_enabler, decoder_1_out1);
  and and_3 (and_3_out, Write_enabler, decoder_1_out2);
  and and_4 (and_4_out, Write_enabler, decoder_1_out3);
  and and_5 (and_5_out, Write_enabler, decoder_1_out4);
  and and_6 (and_6_out, Write_enabler, decoder_1_out5);
  and and_7 (and_7_out, Write_enabler, decoder_1_out6);
  and and_8 (and_8_out, Write_enabler, decoder_1_out7);
  and and_9 (and_9_out, Write_enabler, decoder_1_out8);
  and and_10 (and_10_out, Write_enabler, decoder_1_out9);
  and and_11 (and_11_out, Write_enabler, decoder_1_out10);
  and and_12 (and_12_out, Write_enabler, decoder_1_out11);
  and and_13 (and_13_out, Write_enabler, decoder_1_out12);
  and and_14 (and_14_out, Write_enabler, decoder_1_out13);
  and and_15 (and_15_out, Write_enabler, decoder_1_out14);
  and and_16 (and_16_out, Write_enabler, decoder_1_out15);
  and and_17 (and_17_out, Write_enabler, decoder_1_out16);
  and and_18 (and_18_out, Write_enabler, decoder_1_out17);
  and and_19 (and_19_out, Write_enabler, decoder_1_out18);
  and and_20 (and_20_out, Write_enabler, decoder_1_out19);
  and and_21 (and_21_out, Write_enabler, decoder_1_out20);
  and and_22 (and_22_out, Write_enabler, decoder_1_out21);
  and and_23 (and_23_out, Write_enabler, decoder_1_out22);
  Register #(.width(23)) _0 (.D(Write_data), .en(and_1_out), .Q(_0_q), .clk(Clock), .clr(Clear));
  Register #(.width(23)) _1 (.D(Write_data), .en(and_2_out), .Q(_1_q), .clk(Clock), .clr(Clear));
  Register #(.width(23)) _2 (.D(Write_data), .en(and_3_out), .Q(_2_q), .clk(Clock), .clr(Clear));
  Register #(.width(23)) _3 (.D(Write_data), .en(and_4_out), .Q(_3_q), .clk(Clock), .clr(Clear));
  Register #(.width(23)) _4 (.D(Write_data), .en(and_5_out), .Q(_4_q), .clk(Clock), .clr(Clear));
  Register #(.width(23)) _5 (.D(Write_data), .en(and_6_out), .Q(_5_q), .clk(Clock), .clr(Clear));
  Register #(.width(23)) _6 (.D(Write_data), .en(and_7_out), .Q(_6_q), .clk(Clock), .clr(Clear));
  Register #(.width(23)) _7 (.D(Write_data), .en(and_8_out), .Q(_7_q), .clk(Clock), .clr(Clear));
  Register #(.width(23)) _8 (.D(Write_data), .en(and_9_out), .Q(_8_q), .clk(Clock), .clr(Clear));
  Register #(.width(23)) _9 (.D(Write_data), .en(and_10_out), .Q(_9_q), .clk(Clock), .clr(Clear));
  Register #(.width(23)) _10 (.D(Write_data), .en(and_11_out), .Q(_10_q), .clk(Clock), .clr(Clear));
  Register #(.width(23)) _11 (.D(Write_data), .en(and_12_out), .Q(_11_q), .clk(Clock), .clr(Clear));
  Register #(.width(23)) _12 (.D(Write_data), .en(and_13_out), .Q(_12_q), .clk(Clock), .clr(Clear));
  Register #(.width(23)) _13 (.D(Write_data), .en(and_14_out), .Q(_13_q), .clk(Clock), .clr(Clear));
  Register #(.width(23)) _14 (.D(Write_data), .en(and_15_out), .Q(_14_q), .clk(Clock), .clr(Clear));
  Register #(.width(23)) _15 (.D(Write_data), .en(and_16_out), .Q(_15_q), .clk(Clock), .clr(Clear));
  Register #(.width(23)) _16 (.D(Write_data), .en(and_17_out), .Q(_16_q), .clk(Clock), .clr(Clear));
  Register #(.width(23)) _17 (.D(Write_data), .en(and_18_out), .Q(_17_q), .clk(Clock), .clr(Clear));
  Register #(.width(23)) _18 (.D(Write_data), .en(and_19_out), .Q(_18_q), .clk(Clock), .clr(Clear));
  Register #(.width(23)) _19 (.D(Write_data), .en(and_20_out), .Q(_19_q), .clk(Clock), .clr(Clear));
  Register #(.width(23)) _20 (.D(Write_data), .en(and_21_out), .Q(_20_q), .clk(Clock), .clr(Clear));
  Register #(.width(23)) _21 (.D(Write_data), .en(and_22_out), .Q(_21_q), .clk(Clock), .clr(Clear));
  Register #(.width(23)) _22 (.D(Write_data), .en(and_23_out), .Q(_22_q), .clk(Clock), .clr(Clear));
  Multiplexer #(.select(5), .width(23), .enable("false")) multiplexer_1 (
    .in0(_0_q), .in1(_1_q), .in2(_2_q), .in3(_3_q), .in4(_4_q), .in5(_5_q), .in6(_6_q), .in7(_7_q),
    .in8(_8_q), .in9(_9_q), .in10(_10_q), .in11(_11_q), .in12(_12_q), .in13(_13_q), .in14(_14_q),
    .in15(_15_q), .in16(_16_q), .in17(_17_q), .in18(_18_q), .in19(_19_q), .in20(_20_q), .in21(_21_q),
    .in22(_22_q), .out(Data_1), .sel(RS));  // open: in23, in24, in25, in26, in27, in28, in29, in30, in31
  Multiplexer #(.select(5), .width(23), .enable("false")) multiplexer_2 (
    .in0(_0_q), .in1(_1_q), .in2(_2_q), .in3(_3_q), .in4(_4_q), .in5(_5_q), .in6(_6_q), .in7(_7_q),
    .in8(_8_q), .in9(_9_q), .in10(_10_q), .in11(_11_q), .in12(_12_q), .in13(_13_q), .in14(_14_q),
    .in15(_15_q), .in16(_16_q), .in17(_17_q), .in18(_18_q), .in19(_19_q), .in20(_20_q), .in21(_21_q),
    .in22(_22_q), .out(Data_2), .sel(RT));  // open: in23, in24, in25, in26, in27, in28, in29, in30, in31
endmodule

module _1_bit_ALU (
  input  Cin,
  input  a,
  input  Ain,
  input  b,
  input  [1:0] ALUop,
  input  Bin,
  output Result,
  output Cout
);

  wire adder_1_out, and_1_out, multiplexer_1_out, multiplexer_2_out, not_1_out, not_2_out, or_1_out;

  not not_1 (not_1_out, a);
  not not_2 (not_2_out, b);
  Multiplexer #(.enable("false")) multiplexer_1 (.in0(a), .in1(not_1_out), .out(multiplexer_1_out), .sel(Ain));
  Multiplexer #(.enable("false")) multiplexer_2 (.in0(b), .in1(not_2_out), .out(multiplexer_2_out), .sel(Bin));
  and and_1 (and_1_out, multiplexer_1_out, multiplexer_2_out);
  or or_1 (or_1_out, multiplexer_1_out, multiplexer_2_out);
  Adder #(.width(1)) adder_1 (.a(multiplexer_1_out), .b(multiplexer_2_out), .out(adder_1_out), .cin(Cin), .cout(Cout));
  Multiplexer #(.select(2), .enable("false")) multiplexer_3 (
    .in0(and_1_out), .in1(or_1_out), .in2(adder_1_out), .out(Result), .sel(ALUop));  // open: in3
endmodule

module _23_Bit_ALU (
  input  [22:0] a,
  input  Cin,
  input  [1:0] ALUop,
  input  Ain,
  input  Bin,
  input  [22:0] b,
  output [22:0] Result,
  output Zero_Ditector,
  output Overflow_Ditector
);

  wire undriven_2, undriven_3;
  wire [1:1] undriven;

  _1_bit_ALU u_1_bit_alu_1 (
    .a(a[21]), .Ain(a[15]), .b(a[17]), .Bin(a[12]), .Result(a[7]), .Cout(a[7]), .Cin(a[12]),
    .ALUop({undriven[1], a[9]}));
  // _1_bit_ALU 1_bit_alu_2: pin names not known; wires that end beside it: {ALUop[1], a[21]}, {ALUop[1], a[21]}, {ALUop[1], a[21]}, Bin
  // _1_bit_ALU 1_bit_alu_3: pin names not known; wires that end beside it: Bin, {ALUop[1], a[21]}, Bin
  // _1_bit_ALU 1_bit_alu_4: pin names not known; wires that end beside it: {ALUop[1], a[21]}, {ALUop[1], a[21]}, {ALUop[1], a[21]}, Bin
  _1_bit_ALU u_1_bit_alu_5 (.a(Bin), .Result(a[21]), .Cout(a[21]));  // open: Ain, b, Bin, Cin, ALUop
  // _1_bit_ALU 1_bit_alu_6: pin names not known; wires that end beside it: {ALUop[1], a[21]}, {ALUop[1], a[21]}, {ALUop[1], a[21]}, Bin
  // _1_bit_ALU 1_bit_alu_7: pin names not known; wires that end beside it: {ALUop[1], a[21]}, {ALUop[1], a[21]}, {ALUop[1], a[21]}, Bin
  // _1_bit_ALU 1_bit_alu_8: pin names not known; wires that end beside it: {ALUop[1], a[21]}, {ALUop[1], a[21]}, {ALUop[1], a[21]}, Bin
  // _1_bit_ALU 1_bit_alu_9: pin names not known; wires that end beside it: {ALUop[1], a[21]}, {ALUop[1], a[21]}, {ALUop[1], a[21]}, Bin
  // _1_bit_ALU 1_bit_alu_10: pin names not known; wires that end beside it: {ALUop[1], a[21]}, {ALUop[1], a[21]}, {ALUop[1], a[21]}, Bin
  // _1_bit_ALU 1_bit_alu_11: pin names not known; wires that end beside it: {ALUop[1], a[21]}, {ALUop[1], a[21]}, Bin
  // _1_bit_ALU 1_bit_alu_12: pin names not known; wires that end beside it: {ALUop[1], a[21]}, Bin, {ALUop[1], a[21]}
  // _1_bit_ALU 1_bit_alu_13: pin names not known; wires that end beside it: {ALUop[1], a[21]}, {ALUop[1], a[21]}, Bin
  // _1_bit_ALU 1_bit_alu_14: pin names not known; wires that end beside it: {ALUop[1], a[21]}, {ALUop[1], a[21]}, Bin
  // _1_bit_ALU 1_bit_alu_15: pin names not known; wires that end beside it: {ALUop[1], a[21]}, {ALUop[1], a[21]}, Bin
  _1_bit_ALU u_1_bit_alu_16 (.Cin(a[21]));  // open: a, Ain, b, Bin, Result, Cout, ALUop
  _1_bit_ALU u_1_bit_alu_17 (.Result(a[21]), .Cout(a[21]));  // open: a, Ain, b, Bin, Cin, ALUop
  // _1_bit_ALU 1_bit_alu_18: pin names not known; wires that end beside it: {ALUop[1], a[21]}, {ALUop[1], a[21]}, {ALUop[1], a[21]}, Bin
  _1_bit_ALU u_1_bit_alu_19 (.a(a[21]));  // open: Ain, b, Bin, Result, Cout, Cin, ALUop
  // _1_bit_ALU 1_bit_alu_20: pin names not known; wires that end beside it: {ALUop[1], a[21]}, {ALUop[1], a[21]}, Bin
  // _1_bit_ALU 1_bit_alu_21: pin names not known; wires that end beside it: {ALUop[1], a[21]}, {ALUop[1], a[21]}, Bin
  _1_bit_ALU u_1_bit_alu_22 (.Result(a[21]), .Cout(a[21]));  // open: a, Ain, b, Bin, Cin, ALUop
  // _1_bit_ALU 1_bit_alu_23: pin names not known; wires that end beside it: {ALUop[1], a[21]}, {ALUop[1], a[21]}, Bin
  xor xor_1 (Overflow_Ditector, undriven_2, undriven_3);
  nor nor_1 (Zero_Ditector, Result[0], Result[1], Result[2], Result[3], Result[4], Result[5], Result[6], Result[7], Result[8], Result[9], Result[10], Result[11], Result[12], Result[13], Result[14], Result[15], Result[16], Result[17], Result[18], Result[19], Result[20], Result[21], Result[22]);
  // Pins of 1 and 2 bits meet at {ALUop[1], a[21]}
  // Pins of 1 and 2 bits meet at {undriven[1], a[9]}

  assign {a[16], a[4], a[2]} = {3{a[21]}};
  assign Ain = a[21];
  assign ALUop[0] = a[21];
endmodule

module pc_again (
  input  in_1,
  input  clr,
  input  a,
  input  in_4,
  input  [22:0] in_5
);

  wire and_1_out, bit_extender_4_out, clock_1_out, control_unit_1_aluop0, control_unit_1_aluop1,
       control_unit_1_alusrc, control_unit_1_branch, control_unit_1_jump, control_unit_1_memread,
       control_unit_1_memtoreg, control_unit_1_memwrite, control_unit_1_regdest, control_unit_1_regwrite,
       n23_bit_alu_1_zero_ditector;
  wire [2:0] bit_extender_6_out, rom_1_data;
  wire [3:0] bit_extender_5_out;
  wire [4:0] multiplexer_2_out;
  wire [9:0] rom_1_data_2;
  wire [19:10] rom_1_data_3;
  wire [22:0] adder_1_out, bit_extender_1_out, bit_extender_2_out, bit_extender_3_out, multiplexer_1_out,
       multiplexer_3_out, multiplexer_4_out, multiplexer_5_out, ram_1_data, register_1_q,
       register_file_23_1_data_1, register_file_23_1_data_2;

  Clock clock_1 (.out(clock_1_out));
  assign bit_extender_1_out = {{22{1'b0}}, 1'b1};  // Bit_Extender bit_extender_1
  Register #(.width(23)) register_1 (
    .D(multiplexer_3_out), .Q(register_1_q), .clk(clock_1_out), .clr(in_4));  // open: en
  assign bit_extender_2_out = {{13{1'b0}}, rom_1_data_2};  // Bit_Extender bit_extender_2
  Adder #(.width(23)) adder_1 (.a(bit_extender_1_out), .b(register_1_q), .out(adder_1_out));  // open: cin, cout
  ROM #(.addrWidth(23), .dataWidth(23)) rom_1 (
    .addr(register_1_q), .data({rom_1_data, rom_1_data_3, rom_1_data_2}));  // open: sel
  control_unit control_unit_1 (
    .in_1(rom_1_data), .RegDest(control_unit_1_regdest), .RegWrite(control_unit_1_regwrite),
    .AluSrc(control_unit_1_alusrc), .MemRead(control_unit_1_memread), .MemToReg(control_unit_1_memtoreg),
    .MemWrite(control_unit_1_memwrite), .Branch(control_unit_1_branch), .AluOp1(control_unit_1_aluop1),
    .JUMP(control_unit_1_jump), .AluOp0(control_unit_1_aluop0));
  Multiplexer #(.width(23), .enable("false")) multiplexer_1 (
    .in0(adder_1_out), .in1(bit_extender_2_out), .out(multiplexer_1_out), .sel(and_1_out));
  assign bit_extender_3_out = {{4{1'b0}}, {rom_1_data_3[18:10], rom_1_data_2}};  // Bit_Extender bit_extender_3
  Bit_Extender #(.in_width(5), .out_width(1)) bit_extender_4 (.in(rom_1_data_2[9:5]), .out(bit_extender_4_out));
  Multiplexer #(.width(5), .enable("false")) multiplexer_2 (
    .in0(rom_1_data_2[9:5]), .in1(rom_1_data_3[14:10]), .out(multiplexer_2_out), .sel(control_unit_1_regdest));
  assign bit_extender_5_out = {{3{1'b0}}, control_unit_1_jump};  // Bit_Extender bit_extender_5
  assign bit_extender_6_out = {{2{1'b0}}, control_unit_1_aluop0};  // Bit_Extender bit_extender_6
  Multiplexer #(.width(23), .enable("false")) multiplexer_3 (
    .in0(multiplexer_1_out), .in1(bit_extender_3_out), .out(multiplexer_3_out), .sel(control_unit_1_aluop1));
  register_file_23 register_file_23_1 (
    .Write_data(multiplexer_5_out), .Write_enabler(control_unit_1_regwrite), .RD(multiplexer_2_out),
    .Clock(clock_1_out), .Data_1(register_file_23_1_data_1), .RS(rom_1_data_3[19:15]),
    .Data_2(register_file_23_1_data_2), .RT(rom_1_data_3[14:10]), .Clear(a));
  Multiplexer #(.width(23), .enable("false")) multiplexer_4 (
    .in0(register_file_23_1_data_1), .in1(bit_extender_2_out), .out(multiplexer_4_out),
    .sel(control_unit_1_alusrc));
  alu_control alu_control_1 (.in_1(bit_extender_5_out), .in_2(bit_extender_6_out));  // open: in_3
  and and_1 (and_1_out, control_unit_1_branch, n23_bit_alu_1_zero_ditector);
  _23_Bit_ALU u_23_bit_alu_1 (
    .Result(in_5), .a(register_file_23_1_data_2), .Ain(bit_extender_4_out), .b(multiplexer_4_out),
    .Zero_Ditector(n23_bit_alu_1_zero_ditector), .Overflow_Ditector(in_1));  // open: ALUop, Bin, Cin
  RAM #(.addrWidth(23), .dataWidth(23), .bus("separate")) ram_1 (
    .addr(in_5), .din(register_file_23_1_data_1), .data(ram_1_data), .str(control_unit_1_memwrite),
    .clk(clock_1_out), .ld(control_unit_1_memread), .clr(clr));  // open: sel
  Multiplexer #(.width(23), .enable("false")) multiplexer_5 (
    .in0(in_5), .in1(ram_1_data), .out(multiplexer_5_out), .sel(control_unit_1_memtoreg));

  // Notes on the sheet:
  //   contents of rom_1 (hex, n*v repeats v):
  //   20300 20400 20500 20500 15600
  //   func
  //   shft
  //   RD
  //   RT
  //   RS
endmodule

module control_unit (
  input  [2:0] in_1,
  output RegDest,
  output RegWrite,
  output AluSrc,
  output MemRead,
  output MemToReg,
  output MemWrite,
  output Branch,
  output AluOp1,
  output JUMP,
  output AluOp0
);

  wire not_1_out, not_2_out, not_3_out, not_4_out, not_5_out, not_6_out, not_7_out, not_8_out, not_9_out,
       not_10_out, not_11_out;

  not not_1 (not_1_out, in_1[0]);
  not not_2 (not_2_out, in_1[0]);
  not not_3 (not_3_out, in_1[1]);
  not not_4 (not_4_out, in_1[2]);
  and and_1 (AluOp1, not_1_out, not_2_out, not_3_out, not_4_out);
  not not_5 (not_5_out, in_1[2]);
  not not_6 (not_6_out, in_1[1]);
  not not_7 (not_7_out, in_1[0]);
  and and_2 (MemRead, not_5_out, not_6_out, not_7_out, in_1[0]);
  not not_8 (not_8_out, in_1[1]);
  and and_3 (MemWrite, in_1[0], in_1[0], not_8_out, in_1[2]);
  not not_9 (not_9_out, in_1[1]);
  not not_10 (not_10_out, in_1[2]);
  and and_4 (AluOp0, in_1[0], in_1[0], not_9_out, not_10_out);
  not not_11 (not_11_out, in_1[0]);
  and and_5 (JUMP, not_11_out, in_1[1], in_1[2]);
  or or_1 (RegWrite, AluOp1, MemRead);
  or or_2 (AluSrc, MemRead, MemWrite);

  assign Branch = AluOp0;
  assign MemToReg = MemRead;
  assign RegDest = AluOp1;

  // Notes on the sheet:
  //   0000
  //   R Type
  //   0001
  //   LW
  //   0010
  //   SW
  //   0011
  //   BEQ
  //   0100
  //   JUMP
endmodule

module alu_control (
  input  [3:0] in_1,
  input  [2:0] in_2,
  input  [2:0] in_3
);

  wire and_3_out;

  and and_1 (in_3[0], in_2[2], in_1[3]);
  and and_2 (in_3[1], in_2[2], in_1[2]);
  and and_3 (and_3_out, in_2[2], in_1[1]);
  or or_1 (in_3[2], and_3_out, in_2[0]);
endmodule
